// Logisim project Main_Circuit_16_bit_CPU_Pipelined.circ as structural Verilog: 21 circuits, main circuit Pipelined_CPU
module Single_Cycle_Processor (
  output [15:0] Write_Reg,
  output [15:0] out_2,
  output [15:0] out_3,
  output [15:0] out_4,
  output [15:0] out_5,
  output [15:0] out_6,
  output [15:0] out_7,
  output [15:0] out_8,
  output [15:0] out_9
);

  wire Branch, Branch_inst, Clear, clock_1_out, Comp, Main_Control_alusrc, Main_Control_extop, Mov_Taken,
       or_1_out, SW, Write_Enb;
  wire [1:0] Main_Control_regtype, Main_Control_wbdata, Pipelined_PC_Control_p3;
  wire [2:0] multiplexer_2_out, multiplexer_3_out;
  wire [6:0] ALUOp;
  wire [11:0] adder_2_out, multiplexer_1_out, PC_Next, PC_pc_address;
  wire [11:3] Instruction_Memory_instruction;
  wire [15:0] ALU_alu_output, bit_extender_2_out, data_memory_1_word, Imm, multiplexer_4_out,
       register_file_1_busa, Rs, shifter_1_out;

  // PC_Select Pipelined_PC_Control: pin names not known; wires that end beside it: Branch, ALUOp[6:3], Pipelined_PC_Control_p3, Comp, ALUOp[2:0], Branch_inst
  Clock clock_1 (.out(clock_1_out));
  Multiplexer #(.select(2), .width(12)) multiplexer_1 (
    .in0(PC_Next), .in1(adder_2_out), .in2(Imm[11:0]), .in3(Rs[11:0]), .out(multiplexer_1_out),
    .sel(Pipelined_PC_Control_p3));  // open: en
  PC PC (.PC_Reg(multiplexer_1_out), .PC_Address(PC_pc_address), .Clk(clock_1_out), .Clear(Clear));  // open: Stall
  Adder #(.width(12)) adder_1 (.a(12'h1), .b(PC_pc_address), .out(PC_Next));  // open: cin, cout
  Adder #(.width(12)) adder_2 (.a(PC_Next), .b(Imm[11:0]), .out(adder_2_out));  // open: cin, cout
  Instruction_Memory Instruction_Memory (
    .PC_Address(PC_pc_address), .Instruction({ALUOp[6:3], Instruction_Memory_instruction, ALUOp[2:0]}),
    .Clk(clock_1_out));  // open: Stall
  Bit_Extender bit_extender_1 (
    .Imm({Instruction_Memory_instruction[5:3], ALUOp[2:0]}), .ImmExt(Imm), .ExtOp(Main_Control_extop));
  Main_control Main_Control (
    .op(ALUOp[6:3]), .Branch_inst(Branch_inst), .func(ALUOp[2:0]), .Mem_Write(SW),
    .ExtOp(Main_Control_extop), .RegType(Main_Control_regtype), .ALUSrc(Main_Control_alusrc),
    .WBData(Main_Control_wbdata));  // open: Mem_Write_2, LW, Kill2
  or or_1 (or_1_out, Branch_inst, SW);
  Multiplexer #(.width(3)) multiplexer_2 (
    .in0(Instruction_Memory_instruction[5:3]), .in1(Instruction_Memory_instruction[11:9]),
    .out(multiplexer_2_out), .sel(or_1_out));  // open: en
  Multiplexer #(.select(2), .width(3)) multiplexer_3 (
    .in0(Instruction_Memory_instruction[11:9]), .in1(Instruction_Memory_instruction[11:9]), .in2(3'b001),
    .in3(3'b111), .out(multiplexer_3_out), .sel(Main_Control_regtype));  // open: en
  Button u_Clear (.out(Clear));
  Reg_Write_Sel Reg_Write_Sel (.op(ALUOp[6:3]), .Mem_Write(Write_Enb), .func(ALUOp[2:0]), .Mov_Taken(Mov_Taken));
  Register_File register_file_1 (
    .Bus_Write(Write_Reg), .Clk(clock_1_out), .Clear(Clear), .Write_En(Write_Enb),
    .Reg_Write(multiplexer_3_out), .BusA(register_file_1_busa), .RegA(multiplexer_2_out), .BusB(Rs),
    .RegB(Instruction_Memory_instruction[8:6]), .Reg_0(out_2), .Reg_1(out_4), .Reg_3(out_8), .Reg_2(out_6),
    .Reg_4(out_3), .Reg_5(out_5), .Reg_6(out_7), .Reg_7(out_9));
  Multiplexer #(.width(16)) multiplexer_4 (
    .in0(register_file_1_busa), .in1(Imm), .out(multiplexer_4_out), .sel(Main_Control_alusrc));  // open: en
  ALU ALU (
    .Mov_Taken(Mov_Taken), .Rs(Rs), .ALU_Output(ALU_alu_output), .Rt_Imm(multiplexer_4_out),
    .Comparison(Comp), .ALUOp(ALUOp));
  Data_Memory data_memory_1 (
    .Word_Address(ALU_alu_output), .MemWr(SW), .MemRd(1'b1), .Word(data_memory_1_word), .Clk(clock_1_out),
    .Rt(register_file_1_busa));
  Shifter #(.width(16)) shifter_1 (.in(Imm), .\dist (4'b0100), .out(shifter_1_out));
  assign bit_extender_2_out = {{4{1'b0}}, PC_Next};  // Bit_Extender_part bit_extender_2
  Multiplexer #(.select(2), .width(16)) multiplexer_5 (
    .in0(ALU_alu_output), .in1(bit_extender_2_out), .in2(shifter_1_out), .in3(data_memory_1_word),
    .out(Write_Reg), .sel(Main_Control_wbdata));  // open: en

  // Other names for the same wires on the sheet: func[2:0] = ALUOp[2:0]; op[3:0] = ALUOp[6:3];
  //   Imm_12[11:0] = Imm[11:0]; r0[15:0] = out_2; r1[15:0] = out_4; r2[15:0] = out_6; r3[15:0] = out_8;
  //   r4[15:0] = out_3; r5[15:0] = out_5; r6[15:0] = out_7; r7[15:0] = out_9; Rs_12[11:0] = Rs[11:0]

  // Notes on the sheet:
  //   Registers
  //   Branch Offset
  //   RegType
  //   ALUSrc
  //   MemWr
  //   MemRd
  //   WBData
endmodule

module Register_File (
  input  [15:0] Bus_Write,
  input  Clk,
  input  Clear,
  input  Write_En,
  input  [2:0] Reg_Write,
  input  [2:0] RegA,
  input  [2:0] RegB,
  output [15:0] Reg_0,
  output [15:0] Reg_1,
  output [15:0] Reg_2,
  output [15:0] Reg_3,
  output [15:0] Reg_4,
  output [15:0] Reg_5,
  output [15:0] BusA,
  output [15:0] BusB,
  output [15:0] Reg_6,
  output [15:0] Reg_7
);

  wire and_1_out, and_2_out, and_3_out, and_4_out, and_5_out, and_6_out, and_7_out, decoder_1_out1,
       decoder_1_out2, decoder_1_out3, decoder_1_out4, decoder_1_out5, decoder_1_out6, decoder_1_out7;

  Decoder #(.select(3)) decoder_1 (
    .out1(decoder_1_out1), .out2(decoder_1_out2), .out3(decoder_1_out3), .out4(decoder_1_out4),
    .out5(decoder_1_out5), .out6(decoder_1_out6), .out7(decoder_1_out7), .sel(Reg_Write), .en(1'b1));  // open: out0
  Register #(.width(16)) Zero_Register (.D(Bus_Write), .en(1'b0), .Q(Reg_0), .clk(Clk), .clr(Clear));
  Register #(.width(16)) register_1 (.D(Bus_Write), .en(and_1_out), .Q(Reg_1), .clk(Clk), .clr(Clear));
  and and_1 (and_1_out, Write_En, decoder_1_out1);
  Register #(.width(16)) register_2 (.D(Bus_Write), .en(and_2_out), .Q(Reg_2), .clk(Clk), .clr(Clear));
  and and_2 (and_2_out, Write_En, decoder_1_out2);
  Register #(.width(16)) register_3 (.D(Bus_Write), .en(and_3_out), .Q(Reg_3), .clk(Clk), .clr(Clear));
  and and_3 (and_3_out, Write_En, decoder_1_out3);
  Register #(.width(16)) register_4 (.D(Bus_Write), .en(and_4_out), .Q(Reg_4), .clk(Clk), .clr(Clear));
  and and_4 (and_4_out, Write_En, decoder_1_out4);
  Register #(.width(16)) register_5 (.D(Bus_Write), .en(and_5_out), .Q(Reg_5), .clk(Clk), .clr(Clear));
  and and_5 (and_5_out, Write_En, decoder_1_out5);
  Register #(.width(16)) register_6 (.D(Bus_Write), .en(and_6_out), .Q(Reg_6), .clk(Clk), .clr(Clear));
  and and_6 (and_6_out, Write_En, decoder_1_out6);
  Register #(.width(16)) register_7 (.D(Bus_Write), .en(and_7_out), .Q(Reg_7), .clk(Clk), .clr(Clear));
  and and_7 (and_7_out, Write_En, decoder_1_out7);
  Multiplexer #(.select(3), .width(16)) multiplexer_1 (
    .in0(Reg_0), .in1(Reg_1), .in2(Reg_2), .in3(Reg_3), .in4(Reg_4), .in5(Reg_5), .in6(Reg_6), .in7(Reg_7),
    .out(BusA), .sel(RegA));  // open: en
  Multiplexer #(.select(3), .width(16)) multiplexer_2 (
    .in0(Reg_0), .in1(Reg_1), .in2(Reg_2), .in3(Reg_3), .in4(Reg_4), .in5(Reg_5), .in6(Reg_6), .in7(Reg_7),
    .out(BusB), .sel(RegB));  // open: en
endmodule

module ALU (
  input  [15:0] Rs,
  input  [15:0] Rt_Imm,
  input  [6:0] ALUOp,
  output Mov_Taken,
  output [15:0] ALU_Output,
  output Comparison
);

  wire Add_Sub_Sel_s, adder_1_cout, comparator_op_1_comp_out, invert_comp_1_invert, Movn_Movz_movn_taken,
       Movn_Movz_movz_taken;
  wire [1:0] ALU_Sel_alu_sel, Comparison_Sel_comp_sel, Logic_Sel_s1s0;
  wire [15:0] adder_1_out, and_1_out, bit_extender_1_out, bit_extender_2_out, Movn_Movz_movn, Movn_Movz_movz,
       multiplexer_2_out, multiplexer_3_out, multiplexer_4_out, not_1_out, or_1_out, Shifter_shift_out,
       xor_1_out, xor_2_out;

  Add_Sub_Select Add_Sub_Sel (.op(ALUOp[6:3]), .func(ALUOp[2:0]), .S(Add_Sub_Sel_s));
  assign and_1_out = Rs & Rt_Imm;  // AND_Gate and_1, 16 bits wide
  assign xor_1_out = Rs ^ Rt_Imm;  // XOR_Gate xor_1, 16 bits wide
  Shifter_Circuit Shifter (.func(ALUOp[2:0]), .Rt(Rt_Imm), .Shift_Out(Shifter_shift_out), .Rs(Rs));
  Mov_Op Movn_Movz (
    .Movz_Taken(Movn_Movz_movz_taken), .Rt(Rt_Imm), .Rs(Rs), .MOVN(Movn_Movz_movn), .MOVZ(Movn_Movz_movz),
    .ALUOp(ALUOp), .Movn_Taken(Movn_Movz_movn_taken));
  assign bit_extender_1_out = {{15{Add_Sub_Sel_s}}, Add_Sub_Sel_s};  // Bit_Extender_part bit_extender_1
  assign xor_2_out = bit_extender_1_out ^ Rt_Imm;  // XOR_Gate xor_2, 16 bits wide
  assign or_1_out = Rs | Rt_Imm;  // OR_Gate or_1, 16 bits wide
  Multiplexer multiplexer_1 (
    .in0(Movn_Movz_movz_taken), .in1(Movn_Movz_movn_taken), .out(Mov_Taken), .sel(ALUOp[0]));  // open: en
  Multiplexer #(.width(16)) multiplexer_2 (
    .in0(Movn_Movz_movz), .in1(Movn_Movz_movn), .out(multiplexer_2_out), .sel(ALUOp[0]));  // open: en
  Adder #(.width(16)) adder_1 (.a(Rs), .b(xor_2_out), .out(adder_1_out), .cin(Add_Sub_Sel_s), .cout(adder_1_cout));
  Comp_Select Comparison_Sel (.Op(ALUOp[6:3]), .Comp_Sel(Comparison_Sel_comp_sel), .Func(ALUOp[2:0]));
  Multiplexer #(.select(2), .width(16)) multiplexer_3 (
    .in0(or_1_out), .in1(and_1_out), .in2(not_1_out), .in3(xor_1_out), .out(multiplexer_3_out),
    .sel(Logic_Sel_s1s0));  // open: en
  assign not_1_out = ~and_1_out;  // NOT_Gate not_1, 16 bits wide
  Logic_Select Logic_Sel (.S1S0(Logic_Sel_s1s0), .Op(ALUOp[6:3]), .Func(ALUOp[2:0]));
  Comparator_Op comparator_op_1 (
    .Overflow_Carry(adder_1_cout), .Comp_Out(comparator_op_1_comp_out),
    .Comp_Select(Comparison_Sel_comp_sel), .Arith_Out(adder_1_out), .InputA(Rs), .InputB(Rt_Imm));
  Multiplexer #(.width(16)) multiplexer_4 (
    .in0(Shifter_shift_out), .in1(multiplexer_2_out), .out(multiplexer_4_out), .sel(ALUOp[2]));  // open: en
  Invert_Comp invert_comp_1 (.invert(invert_comp_1_invert), .Op(ALUOp[6:3]), .Func(ALUOp[2:0]));
  xor xor_3 (Comparison, comparator_op_1_comp_out, invert_comp_1_invert);
  assign bit_extender_2_out = {{15{1'b0}}, Comparison};  // Bit_Extender_part bit_extender_2
  ALU_Select ALU_Sel (.Op(ALUOp[6:3]), .Func(ALUOp[2:0]), .ALU_Sel(ALU_Sel_alu_sel));
  Multiplexer #(.select(2), .width(16)) multiplexer_5 (
    .in0(multiplexer_4_out), .in1(adder_1_out), .in2(bit_extender_2_out), .in3(multiplexer_3_out),
    .out(ALU_Output), .sel(ALU_Sel_alu_sel));  // open: en

  // Other names for the same wires on the sheet: func[2:0] = ALUOp[2:0]; InputA[15:0] = Rs; InputB[15:0] = Rt_Imm;
  //   op[3:0] = ALUOp[6:3]

  // Notes on the sheet:
  //   Logic Op
  //   Shift/Mov Op
endmodule

module Logic_Select (
  input  [3:0] Op,
  input  [2:0] Func,
  output [1:0] S1S0
);

  wire and_2_out, and_3_out, not_1_out, not_2_out;

  not not_1 (not_1_out, Op[1]);
  not not_2 (not_2_out, Op[0]);
  and and_1 (S1S0[1], not_1_out, Func[1]);
  and and_2 (and_2_out, not_1_out, Func[0]);
  and and_3 (and_3_out, Op[1], not_2_out);
  or or_1 (S1S0[0], and_2_out, and_3_out);
endmodule

module Add_Sub_Select (
  input  [3:0] op,
  input  [2:0] func,
  output S
);

  wire and_1_out, and_2_out, and_3_out, not_1_out, not_2_out, not_3_out, not_4_out, not_5_out, not_6_out,
       xor_1_out;

  xor xor_1 (xor_1_out, op[0], op[1]);
  and and_1 (and_1_out, xor_1_out, op[2], not_4_out);
  nor nor_1 (S, and_1_out, and_2_out, and_3_out);
  not not_1 (not_1_out, func[0]);
  not not_2 (not_2_out, func[1]);
  and and_2 (and_2_out, not_5_out, op[2], not_3_out, not_4_out);
  not not_3 (not_3_out, op[1]);
  not not_4 (not_4_out, op[3]);
  not not_5 (not_5_out, op[0]);
  not not_6 (not_6_out, op[2]);
  and and_3 (and_3_out, not_1_out, not_2_out, func[2], not_5_out, not_3_out, not_6_out, not_4_out);
endmodule

module Comparator_Op (
  input  Overflow_Carry,
  input  [1:0] Comp_Select,
  input  [15:0] Arith_Out,
  input  [15:0] InputA,
  input  [15:0] InputB,
  output Comp_Out
);

  wire A_GE_B, and_1_out, and_2_out, and_3_out, bitselector_1_out, bitselector_2_out, bitselector_3_out,
       nor_1_out, not_1_out, not_2_out, not_3_out, or_1_out;

  nor nor_1 (nor_1_out, Arith_Out[0], Arith_Out[1], Arith_Out[2], Arith_Out[3], Arith_Out[4], Arith_Out[5], Arith_Out[6], Arith_Out[7], Arith_Out[8], Arith_Out[9], Arith_Out[10], Arith_Out[11], Arith_Out[12], Arith_Out[13], Arith_Out[14], Arith_Out[15]);
  BitSelector #(.width(16)) bitselector_1 (.in(Arith_Out), .out(bitselector_1_out), .sel(4'b1111));
  BitSelector #(.width(16)) bitselector_2 (.in(InputA), .out(bitselector_2_out), .sel(4'b1111));
  BitSelector #(.width(16)) bitselector_3 (.in(InputB), .out(bitselector_3_out), .sel(4'b1111));
  not not_1 (not_1_out, bitselector_2_out);
  not not_2 (not_2_out, bitselector_1_out);
  not not_3 (not_3_out, nor_1_out);
  and and_1 (and_1_out, not_2_out, not_1_out);
  or or_1 (or_1_out, not_2_out, not_1_out);
  and and_2 (and_2_out, A_GE_B, not_3_out);
  or or_2 (A_GE_B, and_1_out, and_3_out);
  and and_3 (and_3_out, or_1_out, bitselector_3_out);
  Multiplexer #(.select(2)) multiplexer_1 (
    .in0(A_GE_B), .in1(Overflow_Carry), .in2(nor_1_out), .in3(and_2_out), .out(Comp_Out), .sel(Comp_Select));  // open: en

  // Notes on the sheet:
  //   A >= B Unsigned
  //   A = B
  //   A >= B
  //   All REQUIRED comparison operations can be found using these four outputs
  //   The select lines have been selected specifically for optimization purposes
  //   A > B
  //   A >= B (00)
  //   A >= B Unsigned (01)
  //   A = B (10)
  //   A > B (11)
endmodule

module Comp_Select (
  input  [3:0] Op,
  input  [2:0] Func,
  output [1:0] Comp_Sel
);

  wire and_1_out, and_2_out, and_3_out, and_4_out, and_5_out, and_6_out, and_7_out, and_8_out, nor_1_out,
       not_1_out, not_2_out, not_3_out, not_4_out, not_5_out, not_6_out, not_7_out, not_8_out, not_9_out,
       or_2_out, xor_1_out;

  and and_1 (and_1_out, Op[1], not_1_out, Op[3]);
  not not_1 (not_1_out, Op[2]);
  not not_2 (not_2_out, Op[3]);
  not not_3 (not_3_out, Op[0]);
  not not_4 (not_4_out, Op[1]);
  not not_5 (not_5_out, Op[2]);
  xor xor_1 (xor_1_out, Op[0], Op[2]);
  nor nor_1 (nor_1_out, Op[0], Op[1], Op[2], Op[3]);
  and and_2 (and_2_out, Func[0], Func[1], Func[2]);
  and and_3 (and_3_out, Op[0], Op[1], Op[2], not_2_out);
  not not_6 (not_6_out, Op[1]);
  not not_7 (not_7_out, Op[2]);
  not not_8 (not_8_out, Op[3]);
  and and_4 (and_4_out, not_3_out, not_4_out, not_5_out, Op[3]);
  and and_5 (and_5_out, not_4_out, Op[3], xor_1_out);
  and and_6 (and_6_out, nor_1_out, and_2_out);
  and and_7 (and_7_out, nor_1_out, not_9_out);
  not not_9 (not_9_out, and_2_out);
  and and_8 (and_8_out, Op[0], not_6_out, not_7_out, not_8_out);
  // OR_Gate or_1 has open pins: in0=and_7_out, in1=and_1_out, out=open
  or or_2 (or_2_out, and_3_out, and_8_out, and_4_out);
  Priority_Encoder #(.select(2)) priority_encoder_1 (
    .in0(1'b1), .in1(and_6_out), .in2(or_2_out), .in3(and_5_out), .out(Comp_Sel), .en_in(1'b1));  // open: gs, en_out
endmodule

module Invert_Comp (
  input  [3:0] Op,
  input  [2:0] Func,
  output invert
);

  wire and_1_out, and_2_out, not_1_out, not_2_out, not_3_out, or_1_out;

  not not_1 (not_1_out, Op[3]);
  not not_2 (not_2_out, Op[2]);
  not not_3 (not_3_out, Op[1]);
  and and_1 (and_1_out, Op[0], Op[1]);
  not not_4 (Func[0], Func[1]);
  or or_1 (or_1_out, and_1_out, Op[2]);
  and and_2 (and_2_out, Func[0], Func[0], Func[2], Op[0], not_3_out, not_2_out, not_1_out);
  or or_2 (invert, or_1_out, and_2_out);
endmodule

module Shifter_Circuit (
  input  [2:0] func,
  input  [15:0] Rt,
  input  [15:0] Rs,
  output [15:0] Shift_Out
);

  wire [15:0] shifter_1_out, shifter_2_out, shifter_3_out, shifter_4_out;

  Shifter #(.width(16)) shifter_1 (.in(Rs), .\dist (Rt[3:0]), .out(shifter_1_out));
  Shifter #(.width(16), .shift("lr")) shifter_2 (.in(Rs), .\dist (Rt[3:0]), .out(shifter_2_out));
  Shifter #(.width(16), .shift("ar")) shifter_3 (.in(Rs), .\dist (Rt[3:0]), .out(shifter_3_out));
  Shifter #(.width(16), .shift("rr")) shifter_4 (.in(Rs), .\dist (Rt[3:0]), .out(shifter_4_out));
  Multiplexer #(.select(2), .width(16)) multiplexer_1 (
    .in0(shifter_1_out), .in1(shifter_2_out), .in2(shifter_3_out), .in3(shifter_4_out), .out(Shift_Out),
    .sel(func[1:0]));  // open: en
endmodule

module ALU_Select (
  input  [3:0] Op,
  input  [2:0] Func,
  output [1:0] ALU_Sel
);

  wire and_2_out, and_4_out, and_5_out, Imm_Add, not_1_out, not_2_out, not_3_out, not_4_out, not_5_out,
       not_6_out, not_7_out, not_8_out, not_9_out, not_10_out, or_1_out, or_2_out, or_3_out, or_4_out,
       or_5_out;

  not not_1 (not_1_out, Op[2]);
  not not_2 (not_2_out, Func[2]);
  or or_1 (or_1_out, Op[0], Op[1], Op[2], Op[3]);
  or or_2 (or_2_out, Func[1], not_2_out, or_1_out);
  not not_3 (not_3_out, Op[1]);
  or or_3 (or_3_out, Op[1], not_1_out, Op[3]);
  not not_4 (not_4_out, Op[0]);
  or or_4 (or_4_out, Op[3], Op[2], Op[1], not_4_out);
  and and_1 (ALU_Sel[1], or_2_out, Imm_Add, or_4_out);
  or or_5 (or_5_out, Op[3], not_1_out, not_3_out, Op[0]);
  not not_5 (not_5_out, Op[2]);
  not not_6 (not_6_out, Op[3]);
  and and_2 (and_2_out, not_6_out, not_5_out, Op[1]);
  and and_3 (Imm_Add, or_5_out, or_3_out);
  not not_7 (not_7_out, or_1_out);
  and and_4 (and_4_out, not_2_out, not_7_out);
  or or_6 (ALU_Sel[0], and_2_out, and_4_out, and_5_out, not_10_out, not_9_out);
  not not_8 (not_8_out, Func[1]);
  and and_5 (and_5_out, not_7_out, not_8_out, Func[2]);
  not not_9 (not_9_out, or_5_out);
  not not_10 (not_10_out, or_3_out);

  // Notes on the sheet:
  //   S1
  //   S0
endmodule

module Mov_Op (
  input  [15:0] Rt,
  input  [15:0] Rs,
  input  [6:0] ALUOp,
  output Movn_Taken,
  output Movz_Taken,
  output [15:0] MOVN,
  output [15:0] MOVZ
);

  wire not_1_out, Not_Mov, or_1_out, undriven;
  wire [15:0] bit_extender_1_out, not_2_out;

  nand nand_1 (Not_Mov, ~ALUOp[1], ALUOp[2], ALUOp[3], ~ALUOp[4], ~ALUOp[5], ~ALUOp[6]);  // NAND_Gate
  or or_1 (or_1_out, Rt[0], Rt[1], Rt[2], Rt[3], Rt[4], Rt[5], Rt[6], Rt[7], Rt[8], Rt[9], Rt[10], Rt[11], Rt[12], Rt[13], Rt[14], Rt[15]);
  not not_1 (not_1_out, or_1_out);
  assign bit_extender_1_out = {{15{1'b0}}, or_1_out};  // Bit_Extender_part bit_extender_1
  assign not_2_out = ~bit_extender_1_out;  // NOT_Gate not_2, 16 bits wide
  assign MOVZ = Rs & not_2_out;  // AND_Gate and_1, 16 bits wide
  assign MOVN = Rs & bit_extender_1_out;  // AND_Gate and_2, 16 bits wide
  or or_2 (Movn_Taken, Not_Mov, or_1_out);
  or or_3 (Movz_Taken, Not_Mov, not_1_out);
  Register #(.width(2)) register_1 (.clk(undriven));  // open: D, en, Q, clr
  Register #(.width(2)) register_2 (.en(undriven));  // open: D, Q, clk, clr

  // Notes on the sheet:
  //   Taken outputs for deciding whether to write to the memory or not
  //   Rt != 0 (16-bit Extend)
  //   Rt ==0 (16-bit extend)
endmodule

module PC (
  input  [11:0] PC_Reg,
  input  Stall,
  input  Clk,
  input  Clear,
  output [11:0] PC_Address
);

  wire not_1_out;

  not not_1 (not_1_out, Stall);
  Register #(.width(12)) register_1 (.D(PC_Reg), .en(not_1_out), .Q(PC_Address), .clk(Clk), .clr(Clear));
endmodule

module Instruction_Memory (
  input  [11:0] PC_Address,
  input  Stall,
  input  Clk,
  output [15:0] Instruction
);

  wire not_1_out;

  not not_1 (not_1_out, Stall);
  RAM #(.addrWidth(12), .dataWidth(16), .bus("separate")) ram_1 (
    .addr(PC_Address), .data(Instruction), .str(1'b0), .clk(Clk), .ld(not_1_out));  // open: din, sel, clr
endmodule

module Data_Memory (
  input  [15:0] Word_Address,
  input  [15:0] Rt,
  input  MemWr,
  input  MemRd,
  input  Clk,
  output [15:0] Word
);

  RAM #(.addrWidth(12), .dataWidth(16), .bus("separate")) ram_1 (
    .addr(Word_Address[11:0]), .din(Rt), .data(Word), .str(MemWr), .clk(Clk), .ld(MemRd));  // open: sel, clr
endmodule

module Bit_Extender (
  input  [5:0] Imm,
  input  ExtOp,
  output [15:0] ImmExt
);

  wire bitselector_1_out, multiplexer_1_out;

  BitSelector #(.width(6)) bitselector_1 (.in(Imm), .out(bitselector_1_out), .sel(3'b101));
  Multiplexer multiplexer_1 (.in0(1'b0), .in1(bitselector_1_out), .out(multiplexer_1_out), .sel(ExtOp));  // open: en
  assign ImmExt[15:6] = {{9{multiplexer_1_out}}, multiplexer_1_out};  // Bit_Extender_part bit_extender_1

  assign ImmExt[5:0] = Imm;

  // Notes on the sheet:
  //   0 = Zero Extend | 1 = Sign Extend
endmodule

module PC_Select (
  input  [2:0] func,
  input  [3:0] op,
  input  Branch_Taken,
  output [1:0] PC_Sel,
  output Kill1,
  output Kill2,
  output Branch_Inst
);

  wire and_1_out, and_2_out, and_3_out, and_4_out, and_5_out, and_6_out, and_8_out, J_Inst, not_1_out,
       not_2_out, not_3_out, not_4_out, not_5_out, not_6_out, not_7_out;

  not not_1 (not_1_out, op[3]);
  not not_2 (not_2_out, op[2]);
  not not_3 (not_3_out, op[1]);
  and and_1 (and_1_out, not_1_out, not_2_out, not_3_out, op[0], func[2], func[1]);
  not not_4 (not_4_out, op[0]);
  not not_5 (not_5_out, op[1]);
  not not_6 (not_6_out, op[2]);
  not not_7 (not_7_out, op[3]);
  and and_2 (and_2_out, op[3], not_6_out, not_5_out, not_4_out);
  and and_3 (and_3_out, op[3], not_6_out, not_5_out, op[0]);
  and and_4 (and_4_out, op[3], not_6_out, op[1], not_4_out);
  and and_5 (and_5_out, op[3], not_6_out, op[1], op[0]);
  and and_6 (and_6_out, op[3], op[2], not_5_out, not_4_out);
  and and_7 (J_Inst, op[3], op[2], op[1]);
  and and_8 (and_8_out, not_7_out, op[2], op[1], op[0]);
  or or_1 (Branch_Inst, and_8_out, and_2_out, and_3_out, and_4_out, and_5_out, and_6_out);
  or or_2 (Kill1, Branch_Taken, J_Inst);
  Priority_Encoder #(.select(2)) priority_encoder_1 (
    .in0(1'b1), .in1(J_Inst), .in2(and_1_out), .in3(Branch_Taken), .out(PC_Sel));  // open: gs, en_out, en_in

  assign Kill2 = Branch_Taken;

  // Notes on the sheet:
  //   JR_Inst
  //   1100
  //   0001 Op
  //   1000
  //   1001
  //   1010
  //   1011
  //   111X
  //   FOR PIPELINING... ASSUME BRANCH IS NOT TAKEN UNTIL OUTPUT IS DECIDED
  //   00 (Other Inst | PC +  = 1)
  //   01 (J Inst)
  //   10 (JR_Inst)
  //   11 (Branch_Inst) 
endmodule

module Reg_Select (
  input  [3:0] Op,
  output [1:0] Reg_Sel
);

  wire and_1_out, and_2_out, nor_1_out;

  nor nor_1 (nor_1_out, Op[1], Op[2], Op[3]);
  and and_1 (and_1_out, Op[1], Op[2], Op[3]);
  and and_2 (and_2_out, Op[2], Op[3], Op[0]);
  Priority_Encoder #(.select(2)) priority_encoder_1 (
    .in0(1'b1), .in1(nor_1_out), .in2(and_2_out), .in3(and_1_out), .out(Reg_Sel), .en_in(1'b1));  // open: gs, en_out

  // Notes on the sheet:
  //   Rt (00)
  //   Rd (01)
  //   R1 (10)
  //   R7(11)
  //   Rd
  //   R7
  //   R1
  //   Rt
endmodule

module Reg_Write_Sel (
  input  [3:0] op,
  input  [2:0] func,
  input  Mov_Taken,
  output Mem_Write
);

  wire and_1_out, and_2_out, and_4_out, and_5_out, and_6_out, and_7_out, LW, multiplexer_1_out, nand_1_out,
       nand_2_out, not_1_out, not_2_out, not_3_out, not_4_out, not_5_out, not_6_out, not_7_out, not_8_out,
       or_1_out;

  not not_1 (not_1_out, op[1]);
  not not_2 (not_2_out, op[2]);
  not not_3 (not_3_out, op[3]);
  and and_1 (and_1_out, not_3_out, not_2_out, not_1_out, op[0]);
  not not_4 (not_4_out, func[0]);
  and and_2 (and_2_out, not_4_out, func[1], func[2]);
  and and_3 (LW, ~op[0], op[1], op[2], ~op[3]);  // AND_Gate
  nand nand_1 (nand_1_out, and_1_out, and_2_out);
  not not_5 (not_5_out, func[1]);
  not not_6 (not_6_out, op[0]);
  nand nand_2 (nand_2_out, op[2], op[1]);
  and and_4 (and_4_out, op[2], op[0]);
  not not_7 (not_7_out, and_5_out);
  and and_5 (and_5_out, and_1_out, func[2], not_5_out);
  and and_6 (and_6_out, and_5_out, Mov_Taken);
  not not_8 (not_8_out, op[2]);
  Multiplexer multiplexer_1 (.in0(nand_2_out), .in1(and_4_out), .out(multiplexer_1_out), .sel(op[3]));  // open: en
  or or_1 (or_1_out, not_6_out, op[1], not_8_out, op[3]);
  and and_7 (and_7_out, or_1_out, multiplexer_1_out, nand_1_out, not_7_out);
  or or_2 (Mem_Write, and_7_out, LW, and_6_out);

  // Notes on the sheet:
  //   0001 Op
  //   Mov Operation with Condition Satisfied
  //   DO not write in SW or JR or MOV Inst (Unless specified)
  //   NOT JR Inst
  //   Not MOV Inst
  //   Not SW
  //   Write in Memory
endmodule

module Main_control (
  input  [3:0] op,
  input  Branch_inst,
  input  [2:0] func,
  input  Kill2,
  output ALUSrc,
  output Mem_Write,
  output ExtOp,
  output [1:0] RegType,
  output [1:0] WBData,
  output LW,
  output Mem_Write_2
);

  wire ALUSrc_t, and_1_out, and_2_out, and_4_out, and_5_out, and_11_out, and_14_out, and_15_out, and_16_out,
       ExtOp_t, multiplexer_1_out, nand_1_out, nand_2_out, nor_1_out, not_1_out, not_2_out, not_3_out,
       not_4_out, not_5_out, not_6_out, not_7_out, not_8_out, not_9_out, not_10_out, not_11_out, not_12_out,
       not_13_out, not_14_out, not_15_out, not_16_out, not_17_out, or_2_out, or_3_out, or_5_out, SW;
  wire [1:0] bit_extender_1_out, RegType_t, WBData_t;

  or or_1 (ExtOp_t, op[3], op[2]);
  not not_1 (not_1_out, op[3]);
  not not_2 (not_2_out, op[2]);
  not not_3 (not_3_out, op[1]);
  and and_1 (and_1_out, not_1_out, not_2_out, not_3_out, op[0]);
  not not_4 (not_4_out, func[0]);
  and and_2 (and_2_out, not_4_out, func[1], func[2]);
  assign bit_extender_1_out = {{1{Kill2}}, Kill2};  // Bit_Extender_part bit_extender_1
  and and_3 (LW, ~op[0], op[1], op[2], ~op[3]);  // AND_Gate
  nand nand_1 (nand_1_out, op[2], op[1]);
  and and_4 (and_4_out, op[2], op[0]);
  nand nand_2 (nand_2_out, and_1_out, and_2_out);
  and and_5 (and_5_out, and_1_out, func[2], not_5_out);
  not not_5 (not_5_out, func[1]);
  assign RegType = RegType_t & ~bit_extender_1_out;  // AND_Gate and_6, 2 bits wide
  assign WBData = WBData_t & ~bit_extender_1_out;  // AND_Gate and_7, 2 bits wide
  Reg_Select Reg_Sel (.Reg_Sel(RegType_t), .Op(op));
  not not_6 (not_6_out, op[0]);
  not not_7 (not_7_out, op[2]);
  not not_8 (not_8_out, and_5_out);
  and and_8 (ALUSrc, ALUSrc_t, ~Kill2);  // AND_Gate
  and and_9 (Mem_Write, SW, ~Kill2);  // AND_Gate
  and and_10 (ExtOp, ExtOp_t, ~Kill2);  // AND_Gate
  or or_2 (or_2_out, not_6_out, op[1], not_7_out, op[3]);
  Multiplexer multiplexer_1 (.in0(nand_1_out), .in1(and_4_out), .out(multiplexer_1_out), .sel(op[3]));  // open: en
  and and_11 (and_11_out, or_2_out, multiplexer_1_out, nand_2_out, not_8_out);
  and and_12 (ALUSrc_t, or_3_out, or_3_out, not_9_out);
  or or_3 (or_3_out, op[1], op[2], op[3]);
  not not_9 (not_9_out, Branch_inst);
  or or_4 (Mem_Write_2, and_11_out, LW, and_5_out);
  not not_10 (not_10_out, op[3]);
  not not_11 (not_11_out, op[1]);
  not not_12 (not_12_out, op[1]);
  not not_13 (not_13_out, op[1]);
  and and_13 (SW, op[0], not_11_out, op[2], not_10_out);
  not not_14 (not_14_out, op[2]);
  and and_14 (and_14_out, op[0], not_12_out, op[2], op[3]);
  not not_15 (not_15_out, op[1]);
  not not_16 (not_16_out, op[2]);
  not not_17 (not_17_out, op[3]);
  nor nor_1 (nor_1_out, op[0], not_13_out, not_14_out, op[3]);
  and and_15 (and_15_out, op[0], op[1], op[2], op[3]);
  and and_16 (and_16_out, op[0], not_15_out, not_16_out, not_17_out, func[0], func[1], func[2]);
  or or_5 (or_5_out, and_15_out, and_16_out);
  Priority_Encoder #(.select(2)) priority_encoder_1 (
    .in0(1'b1), .in1(or_5_out), .in2(and_14_out), .in3(nor_1_out), .out(WBData_t));  // open: gs, en_out, en_in

  // Notes on the sheet:
  //   Zero for ANDI and ORI. Else Sign or Dont Care 
  //   Sign/Zero Extend
  //   0001 Op
  //   DO not write in SW or JR or MOV Inst (Unless specified)
  //   NOT JR Inst
  //   Not MOV Inst
  //   Not SW
  //   Write in Memory
  //   LUI
  //   SW
  //   Mov Operation with Condition Satisfied
  //   JALR
  //   LW
  //   JAL
endmodule

module Pipelined_CPU (
  output [15:0] op,
  output [15:0] Write_Reg,
  output [15:0] op_2,
  output [15:0] op_3,
  output [15:0] out_5,
  output [15:0] out_6,
  output [15:0] out_7,
  output [15:0] out_8,
  output [15:0] out_9,
  output [15:0] out_10,
  output [3:0] op_4,
  output [15:0] out_12,
  output [15:0] out_13
);

  wire ALUSrc_q, and_3_out, and_4_out, Branch, Branch_inst, Branch_inst_decode, Clear, clock_1_out, Comp,
       Kill1, Kill2, LW, Main_Control_alusrc, Main_Control_extop, Mov_Taken, or_1_out, or_2_out,
       Pipelined_PC_Control_branch_inst, register_6_q, register_7_q, register_8_q, register_10_q,
       register_11_q, SW, Write_Enb;
  wire [1:0] forwarding_1_reg1_forward_sel, forwarding_1_reg1_forward_sel_2, Main_Control_regtype,
       Main_Control_wbdata, Pipelined_PC_Control_pc_sel, register_12_q, register_13_q;
  wire [2:0] func, multiplexer_4_out, RegA, RegB, RegW, RW1_q, RW2_q;
  wire [6:0] ALUOp;
  wire [11:0] adder_2_out, multiplexer_1_out, PC_Next, PC_Next_q, PC_pc_address, register_2_q;
  wire [11:3] Inst_Reg_q;
  wire [15:0] ALU_Output_q, bit_extender_2_out, Data_In_q, data_memory_1_word, Forward1,
       Instruction_Memory_instruction, multiplexer_2_out, multiplexer_6_out, multiplexer_7_out, register_3_q,
       register_4_q, register_5_q, register_file_1_busa, Rs, shifter_1_out;

  PC_Select Pipelined_PC_Control (
    .func(func), .op(op_4), .PC_Sel(Pipelined_PC_Control_pc_sel),
    .Branch_Inst(Pipelined_PC_Control_branch_inst), .Kill1(Kill1), .Kill2(Kill2), .Branch_Taken(Branch));
  and and_1 (Branch_inst_decode, Pipelined_PC_Control_branch_inst, ~Kill2);  // AND_Gate
  Clock clock_1 (.out(clock_1_out));
  Register #(.width(1)) register_1 (.D(Branch_inst_decode), .Q(Branch_inst), .clk(clock_1_out));  // open: en, clr
  Multiplexer #(.select(2), .width(12)) multiplexer_1 (
    .in0(PC_Next), .in1(op_3[11:0]), .in2(Rs[11:0]), .in3(register_2_q), .out(multiplexer_1_out),
    .sel(Pipelined_PC_Control_pc_sel));  // open: en
  and and_2 (Branch, Branch_inst, Comp);
  PC PC (.PC_Reg(multiplexer_1_out), .PC_Address(PC_pc_address), .Clk(clock_1_out), .Clear(Clear), .Stall(and_3_out));
  Register #(.width(12)) u_PC_Next (.D(PC_Next), .Q(PC_Next_q), .clk(clock_1_out));  // open: en, clr
  Adder #(.width(12)) adder_1 (.a(12'h1), .b(PC_pc_address), .out(PC_Next));  // open: cin, cout
  Instruction_Memory Instruction_Memory (
    .PC_Address(PC_pc_address), .Instruction(Instruction_Memory_instruction), .Clk(clock_1_out),
    .Stall(and_3_out));
  Adder #(.width(12)) adder_2 (.a(PC_Next_q), .b(op_3[11:0]), .out(adder_2_out));  // open: cin, cout
  and and_3 (and_3_out, LW, ~Kill2);  // AND_Gate
  Register #(.width(12)) register_2 (.D(adder_2_out), .Q(register_2_q), .clk(clock_1_out));  // open: en, clr
  or or_1 (or_1_out, LW, Kill1);
  Register #(.width(16)) Inst_Reg (
    .D(multiplexer_2_out), .Q({op_4, Inst_Reg_q[11:9], RegB, Inst_Reg_q[5:3], func}), .clk(clock_1_out));  // open: en, clr
  Multiplexer #(.width(16)) multiplexer_2 (
    .in0(Instruction_Memory_instruction), .in1({16{1'b0}}), .out(multiplexer_2_out), .sel(or_1_out));  // open: en
  Bit_Extender bit_extender_1 (.Imm({Inst_Reg_q[5:3], func}), .ImmExt(op_3), .ExtOp(Main_Control_extop));
  Main_control Main_Control (
    .op(op_4), .Branch_inst(Branch_inst_decode), .func(func), .Mem_Write(SW), .ExtOp(Main_Control_extop),
    .RegType(Main_Control_regtype), .ALUSrc(Main_Control_alusrc), .WBData(Main_Control_wbdata),
    .Mem_Write_2(Write_Enb), .LW(LW), .Kill2(Kill2));
  or or_2 (or_2_out, Branch_inst_decode, SW);
  Multiplexer #(.width(3)) multiplexer_3 (
    .in0(Inst_Reg_q[5:3]), .in1(Inst_Reg_q[11:9]), .out(RegA), .sel(or_2_out));  // open: en
  Multiplexer #(.select(2), .width(3)) multiplexer_4 (
    .in0(Inst_Reg_q[11:9]), .in1(Inst_Reg_q[11:9]), .in2(3'b001), .in3(3'b111), .out(multiplexer_4_out),
    .sel(Main_Control_regtype));  // open: en
  Button u_Clear (.out(Clear));
  Register_File register_file_1 (
    .Bus_Write(Write_Reg), .Clk(clock_1_out), .Clear(Clear), .Write_En(register_11_q), .Reg_Write(RegW),
    .BusA(register_file_1_busa), .RegA(RegA), .BusB(Rs), .RegB(RegB), .Reg_0(out_5), .Reg_1(out_7),
    .Reg_3(out_12), .Reg_2(out_9), .Reg_4(out_6), .Reg_5(out_8), .Reg_6(out_10), .Reg_7(out_13));
  Register #(.width(3)) RW1 (.D(multiplexer_4_out), .Q(RW1_q), .clk(clock_1_out));  // open: en, clr
  Register #(.width(1)) ALUSrc (.D(Main_Control_alusrc), .Q(ALUSrc_q), .clk(clock_1_out));  // open: en, clr
  Register #(.width(16)) register_3 (.D(op_3), .Q(register_3_q), .clk(clock_1_out));  // open: en, clr
  Multiplexer #(.width(16)) multiplexer_5 (
    .in0(register_5_q), .in1(register_3_q), .out(op_2), .sel(ALUSrc_q));  // open: en
  Multiplexer #(.select(2), .width(16)) multiplexer_6 (
    .in0(Rs), .in1(Forward1), .in2(op), .in3(Write_Reg), .out(multiplexer_6_out),
    .sel(forwarding_1_reg1_forward_sel_2));  // open: en
  Multiplexer #(.select(2), .width(16)) multiplexer_7 (
    .in0(register_file_1_busa), .in1(Forward1), .in2(op), .in3(Write_Reg), .out(multiplexer_7_out),
    .sel(forwarding_1_reg1_forward_sel));  // open: en
  Forwarding forwarding_1 (
    .RegA_Encoded(RegA), .RW_ALU(RW1_q), .RW_Mem(RW2_q), .RW_WB(RegW), .Ex_WR(and_4_out),
    .Data_WR(register_10_q), .WB_WR(register_11_q), .Reg1_Forward_Sel(forwarding_1_reg1_forward_sel),
    .Reg1_Forward_Sel_2(forwarding_1_reg1_forward_sel_2), .RegB_Encoded(RegB));
  Register #(.width(16)) register_4 (.D(multiplexer_6_out), .Q(register_4_q), .clk(clock_1_out));  // open: en, clr
  ALU ALU (
    .Mov_Taken(Mov_Taken), .Rs(register_4_q), .ALU_Output(Forward1), .Rt_Imm(op_2), .Comparison(Comp),
    .ALUOp(ALUOp));
  Register #(.width(16)) register_5 (.D(multiplexer_7_out), .Q(register_5_q), .clk(clock_1_out));  // open: en, clr
  Register #(.width(1)) register_6 (.D(register_7_q), .Q(register_6_q), .clk(clock_1_out));  // open: en, clr
  Register #(.width(1)) register_7 (.D(SW), .Q(register_7_q), .clk(clock_1_out));  // open: en, clr
  and and_4 (and_4_out, Mov_Taken, register_8_q);
  Register #(.width(1)) register_8 (.D(Write_Enb), .Q(register_8_q), .clk(clock_1_out));  // open: en, clr
  Register #(.width(7)) register_9 (.D({op_4, func}), .Q(ALUOp), .clk(clock_1_out));  // open: en, clr
  Register #(.width(1)) register_10 (.D(and_4_out), .Q(register_10_q), .clk(clock_1_out));  // open: en, clr
  Register #(.width(16)) Data_In (.D(register_5_q), .Q(Data_In_q), .clk(clock_1_out));  // open: en, clr
  Register #(.width(16)) ALU_Output (.D(Forward1), .Q(ALU_Output_q), .clk(clock_1_out));  // open: en, clr
  Data_Memory data_memory_1 (
    .Word_Address(ALU_Output_q), .MemWr(register_6_q), .MemRd(1'b1), .Word(data_memory_1_word),
    .Clk(clock_1_out), .Rt(Data_In_q));
  Register #(.width(3)) RW2 (.D(RW1_q), .Q(RW2_q), .clk(clock_1_out));  // open: en, clr
  Shifter #(.width(16)) shifter_1 (.in(op_3), .\dist (4'b0100), .out(shifter_1_out));
  Register #(.width(1)) register_11 (.D(register_10_q), .Q(register_11_q), .clk(clock_1_out));  // open: en, clr
  assign bit_extender_2_out = {{4{1'b0}}, PC_Next};  // Bit_Extender_part bit_extender_2
  Register #(.width(2)) register_12 (.D(Main_Control_wbdata), .Q(register_12_q), .clk(clock_1_out));  // open: en, clr
  Register #(.width(3)) RW3 (.D(RW2_q), .Q(RegW), .clk(clock_1_out));  // open: en, clr
  Register #(.width(2)) register_13 (.D(register_12_q), .Q(register_13_q), .clk(clock_1_out));  // open: en, clr
  Multiplexer #(.select(2), .width(16)) multiplexer_8 (
    .in0(ALU_Output_q), .in1(bit_extender_2_out), .in2(shifter_1_out), .in3(data_memory_1_word), .out(op),
    .sel(register_13_q));  // open: en
  Register #(.width(16)) register_14 (.D(op), .Q(Write_Reg), .clk(clock_1_out));  // open: en, clr

  // Other names for the same wires on the sheet: op_t[3:0] = op_4; Forward2[15:0] = op; Forward3[15:0] = Write_Reg;
  //   Imm[15:0] = op_3; Imm_12[11:0] = op_3[11:0]; r0[15:0] = out_5; r1[15:0] = out_7; r2[15:0] = out_9;
  //   r3[15:0] = out_12; r4[15:0] = out_6; r5[15:0] = out_8; r6[15:0] = out_10; r7[15:0] = out_13;
  //   Rs_12[11:0] = Rs[11:0]

  // Notes on the sheet:
  //   Registers
  //   Branch Offset
  //   RegType
  //   ALUSrc
  //   MemWr
  //   MemRd
  //   WBData
endmodule

// Forward_Control
module Forwarding (
  input  Ex_WR,
  input  Data_WR,
  input  WB_WR,
  input  [2:0] RegA_Encoded,
  input  [2:0] RW_ALU,
  input  [2:0] RW_Mem,
  input  [2:0] RW_WB,
  input  [2:0] RegB_Encoded,
  output [1:0] Reg1_Forward_Sel,
  output [1:0] Reg1_Forward_Sel_2
);

  wire and_1_out, and_2_out, and_3_out, and_4_out, and_5_out, and_6_out, and_7_out, and_8_out, and_9_out,
       and_10_out, and_11_out, and_12_out, nor_1_out, nor_2_out, nor_3_out, nor_4_out, nor_5_out, nor_6_out,
       or_1_out, or_2_out;
  wire [2:0] xor_1_out, xor_2_out, xor_3_out, xor_4_out, xor_5_out, xor_6_out;

  or or_1 (or_1_out, RegA_Encoded[0], RegA_Encoded[1], RegA_Encoded[2]);
  assign xor_1_out = RegA_Encoded ^ RW_ALU;  // XOR_Gate xor_1, 3 bits wide
  assign xor_2_out = RegA_Encoded ^ RW_Mem;  // XOR_Gate xor_2, 3 bits wide
  assign xor_3_out = RegA_Encoded ^ RW_WB;  // XOR_Gate xor_3, 3 bits wide
  nor nor_1 (nor_1_out, xor_1_out[0], xor_1_out[1], xor_1_out[2]);
  nor nor_2 (nor_2_out, xor_2_out[0], xor_2_out[1], xor_2_out[2]);
  nor nor_3 (nor_3_out, xor_3_out[0], xor_3_out[1], xor_3_out[2]);
  and and_1 (and_1_out, or_1_out, nor_1_out);
  and and_2 (and_2_out, or_1_out, nor_2_out);
  and and_3 (and_3_out, nor_3_out, or_1_out);
  or or_2 (or_2_out, RegB_Encoded[0], RegB_Encoded[1], RegB_Encoded[2]);
  and and_4 (and_4_out, Ex_WR, and_1_out);
  and and_5 (and_5_out, Data_WR, and_2_out);
  and and_6 (and_6_out, WB_WR, and_3_out);
  assign xor_4_out = RegB_Encoded ^ RW_ALU;  // XOR_Gate xor_4, 3 bits wide
  assign xor_5_out = RegB_Encoded ^ RW_Mem;  // XOR_Gate xor_5, 3 bits wide
  assign xor_6_out = RegB_Encoded ^ RW_WB;  // XOR_Gate xor_6, 3 bits wide
  nor nor_4 (nor_4_out, xor_4_out[0], xor_4_out[1], xor_4_out[2]);
  nor nor_5 (nor_5_out, xor_5_out[0], xor_5_out[1], xor_5_out[2]);
  nor nor_6 (nor_6_out, xor_6_out[0], xor_6_out[1], xor_6_out[2]);
  and and_7 (and_7_out, or_2_out, nor_4_out);
  and and_8 (and_8_out, or_2_out, nor_5_out);
  and and_9 (and_9_out, nor_6_out, or_2_out);
  Priority_Encoder #(.select(2)) priority_encoder_1 (
    .in0(1'b1), .in1(and_4_out), .in2(and_5_out), .in3(and_6_out), .out(Reg1_Forward_Sel));  // open: gs, en_out, en_in
  and and_10 (and_10_out, Ex_WR, and_7_out);
  and and_11 (and_11_out, Data_WR, and_8_out);
  and and_12 (and_12_out, WB_WR, and_9_out);
  Priority_Encoder #(.select(2)) priority_encoder_2 (
    .in0(1'b1), .in1(and_10_out), .in2(and_11_out), .in3(and_12_out), .out(Reg1_Forward_Sel_2));  // open: gs, en_out, en_in
endmodule
